# Fritzing sketch circuit (saved by Fritzing 0.9.3b)
breadboards: 1

parts:
  Part1 = Arduino Mega 2560 (Rev3)
  hc-sr1 = hc-sr04
  LED1 = LED - 5mm [color="Red (633nm)" package="5 mm [THT]"]
  LED2 = LED - 5mm [color="Green (565nm)" package="5 mm [THT]"]

nets:
  N1: Part1.D13_PWM, hc-sr1.Trig
  N2: Part1.D12_PWM, hc-sr1.Echo
  N3: Part1.D10_PWM, LED1.anode
  N4: Part1.D9_PWM, LED2.anode
  5V: Part1.5V, hc-sr1.VCC
  GND: Part1.GND, hc-sr1.GND, LED1.cathode, LED2.cathode
